# Fritzing sketch Sigfox+nrf_concept_Fritzing (saved by Fritzing 0.7.12b)
breadboards: 1

parts:
  U1 = atmega328 [package=dip]
  XTAL1 = Crystal [frequency="4 MHz" package=THT]
  C1 = Ceramic Disk Capacitor [package=THT]
  C2 = Ceramic Disk Capacitor [package=THT]
  J1 = Generic female header - 4 pins [package=THT]
  LED1 = green smd LED [package="1206 [SMD]"]
  R2 = Resistor [tolerance=±5% resistance=220 package="1206 [SMD]"]
  J4 = Generic male header - 2 pins [package=THT]
  J3 = double row female pin header, 10 pins [form="♀ (female)"]
  J6 = Generic female header - 6 pins [package=THT]
  J7 = Generic female header [package=THT]
  J8 = Generic male header - 6 pins [package=THT]
  J9 = Generic male header [package=THT]
  J10 = Generic female header [package=THT]
  J11 = Generic female header [package=THT]
  J12 = Generic female header [package=THT]
  J5 = Generic female header - 2 pins [package=THT]
  J13 = Generic female header [package=THT]

nets:
  N1: U1.RESET, J7.pin1
  N2: U1.D0_(RX), J1.pin1
  N3: U1.D1_(TX), J1.pin2
  N4: U1.D2, R2.Pin_0
  N5: U1.D3_(PWM), J4.pin2
  N6: U1.D4, J4.pin1
  N7: U1.VCC, U1.AVCC, J1.pin4, J3.pin5, J3.pin6, J8.pin1, J8.pin2, J8.pin3
  N8: U1.GND, C1.pin_1, C2.pin_1, J1.pin3, LED1.cathode, J8.pin4, J8.pin5, J8.pin6, J11.pin1
  N9: U1.XLAT1, XTAL1.pin_0, C1.pin_0
  N10: U1.XLAT2, XTAL1.pin_1, C2.pin_0
  N11: U1.D5_(PWM), J13.pin1
  N12: U1.D6_(PWM), J5.pin2
  N13: U1.D7, J5.pin1
  N14: U1.D8, J3.pin7
  N15: U1.D9_(PWM), J12.pin1
  N16: U1.D10_(PWM), J3.pin4
  N17: U1.D11_(PWM), J3.pin3
  N18: U1.D12, J3.pin9
  N19: U1.D13, J3.pin8
  N20: U1.AREF, J9.pin1
  N21: U1.A0, J6.pin6
  N22: U1.A1, J6.pin5
  N23: U1.A2, J6.pin4
  N24: U1.A3, J6.pin3
  N25: U1.A4, J6.pin2
  N26: U1.A5, J6.pin1
  N27: LED1.anode, R2.Pin_1
  N28: J3.pin1, J3.pin10, J10.pin1

notes:
  FarmLab
  NRF24L01+
  Sigfox LoRaWAN
  v0.1
